# Fritzing sketch fritzing1 (saved by Fritzing 0.9.3b)
breadboards: 1

parts:
  LED1 = LED - 5mm [color="Red (633nm)" package="5 mm [THT]"]
  R1 = Resistor [tolerance=±5% resistance=220 package=THT]
  LED2 = LED - 5mm [color="Yellow (595nm)" package="5 mm [THT]"]
  R2 = Resistor [tolerance=±5% resistance=220 package=THT]
  LED3 = LED - 5mm [color="Green (565nm)" package="5 mm [THT]"]
  R3 = Resistor [tolerance=±5% resistance=220 package=THT]
  LED4 = LED - 5mm [color="Red (633nm)" package="5 mm [THT]"]
  S1 = Toggle Switch [package=THT]
  R4 = Resistor [tolerance=±5% resistance=220 package=THT]
  Part1 = Arduino Uno (Rev3)
  T1 = LM35 Temperature Sensor [package="TO92 [THT]"]
  Part2 = Humidity Temperature Sensor SHT15

nets:
  GND: LED1.cathode, LED2.cathode, LED3.cathode, Part1.GND, T1.GND, Part2.GND
  N1: LED1.anode, R1.Pin_0
  N2: R1.Pin_1, Part1.D12/MISO
  N3: LED2.anode, R2.Pin_0
  N4: R2.Pin_1, Part1.D11_PWM/MOSI
  N5: LED3.anode, R3.Pin_0
  N6: R3.Pin_1, Part1.D10_PWM/SS
  N7: LED4.cathode, Part1.VIN
  N8: LED4.anode, R4.Pin_0
  N9: S1.L1, R4.Pin_1
  N10: Part1.A0, T1.Vout
  N11: Part1.5V, T1.+Vs
